# Fritzing sketch CanINO (saved by Fritzing 0.9.10b)
breadboards: 1

parts:
  Part1 = Arduino Uno (Rev3)
  U1 = POT [knob_status=50% power=0.5W package=pot_mammoth]
  Grove1 = Grove OLED 128x96
  ZS-042_RTC1 = ZS-042 RTC Module
  Part2 = HX711 Weighing Sensor Module
  S1 = Pushbutton [package="[SMD]"]
  U5 = SWITCH-SPST-2 [package=switch-spst-vertical]
  Load_Cell2 = Load Cell - Red/white/black/green
  Driver2 = 28BYJ-48 Driver Module [part_number=ULN2003 package=THT]
  SM2 = 28BYJ-48 Stepper Motor [part_number=28BYJ-48]

nets:
  N1: Part1.A0, U1.A
  N2: Part1.A4/SDA, Grove1.SCL, ZS-042_RTC1.SDA
  N3: Part1.A5/SCL, Grove1.SDA, ZS-042_RTC1.SCL
  N4: Part1.D8, Driver2.IN1
  N5: Part1.D9_PWM, Driver2.IN2
  N6: Part1.D10_PWM/SS, Driver2.IN3
  N7: Part1.D11_PWM/MOSI, Driver2.IN4
  N8: Part1.D2, U5.P
  N9: Part1.D3_PWM, S1.Pin_3, S1.Pin_4
  N10: Part1.D6_PWM, Part2.DO/RX
  N11: Part1.D7, Part2.CK/TX
  VCC: Part1.5V, U1.S, Grove1.VCC, ZS-042_RTC1.VCC, Part2.VCC, S1.Pin_1, S1.Pin_2, Driver2.Vmotor
  GND: Part1.GND, U1.E, Grove1.GND, ZS-042_RTC1.GND, Part2.GND, U5.O, Driver2.GND
  N12: Part2.E+, Load_Cell2.wire1
  N13: Part2.E-, Load_Cell2.wire3
  N14: Part2.A+, Load_Cell2.wire4
  N15: Part2.A-, Load_Cell2.wire2
  N16: Driver2.blue-pin, SM2.blue-pin
  N17: Driver2.pink-pin, SM2.pink-pin
  N18: Driver2.yellow-pin, SM2.yellow-pin
  N19: Driver2.orange-pin, SM2.orange-pin
  N20: Driver2.red-pin, SM2.red-pin

notes:
  SetupMode

custom parts:
  Load Cell - Red/white/black/green: A rectangle load cell/weighting pressure Sensor with four wires - Red, white, black, green. Normally corresponding with E+, E-, A+, A- respectively.
  28BYJ-48 Driver Module: ULN2003 Driver Module for the 28BYJ-48 Unipolar Stepper Motor LED A - Blue wire - Bottom coil left LED B - Pink wire - Top coil left LED C - Yellow wire - Bottom coil right LED D - Orange wire - Top coil right Common rail - red Connector pins: blue - pink - yellow - orange - red Control pins - IN1 to IN4 Power pins - GND & Vmotor (5-12V) On/Off jumper (if removed, power to motor is cut).
  28BYJ-48 Stepper Motor: Unipolar Stepper Motor 28BYJ-48 Top coil - pink & orange Bottom coil - blue & yellow Common rail - red Connector pins: blue - pink - yellow - orange - red
